# Fritzing sketch SchemaCompleto (saved by Fritzing 0.9.3b)
breadboards: 1

parts:
  Componente1 = Arduino Uno (Rev3)
  S1 = Pushbutton [package="[THT]"]
  R1 = Resistor [tolerance=±5% resistance=1k package=THT]
  S2 = Pushbutton [package="[THT]"]
  R2 = Resistor [tolerance=±5% resistance=1k package=THT]
  S3 = Pushbutton [package="[THT]"]
  S4 = Pushbutton [package="[THT]"]
  R3 = Resistor [tolerance=±5% resistance=1k package=THT]
  R4 = Resistor [tolerance=±5% resistance=1k package=THT]

nets:
  N1: Componente1.D8, S3.Pin_1, S3.Pin_2, R4.Pin_0
  N2: Componente1.D2, S1.Pin_1, S1.Pin_2, R1.Pin_0
  N3: Componente1.D4, S2.Pin_1, S2.Pin_2, R2.Pin_0
  N4: Componente1.D7, S4.Pin_1, S4.Pin_2, R3.Pin_0
  N5: Componente1.5V, S1.Pin_3, S1.Pin_4, S2.Pin_3, S2.Pin_4, S3.Pin_3, S3.Pin_4, S4.Pin_3, S4.Pin_4
  N6: Componente1.GND, R1.Pin_1, R2.Pin_1, R3.Pin_1

notes:
  GND
  +5V
  Alimentatore LED
  Striscia LED NeoPixel
  DIN
  B1
  Legenda:
  B1: Bottone accensione
  B2: Bottone Reset (3s)
  B3: Bottone incremento dell'ora
  B4: Bottone decremento dell'ora
  R1: 1 kOhm
  R2: 1 kOhm
  R3: 1 kOhm
  R4: 1 kOhm
  B2
  R1
  R2
  B3
  B4
  R4
  R3
